# Fritzing sketch skibidi_cuckoo_clock (saved by Fritzing 1.0.2b)
breadboards: 2

parts:
  A1 = Particle - Photon2
  S1 = Pushbutton [package="[THT]"]
  S2 = Pushbutton [package="[THT]"]
  Neopixel1 = Adafruit RBG Smart Neopixel [package="DIP (Dual Inline) [THT]"]
  Neopixel2 = Adafruit RBG Smart Neopixel [package="DIP (Dual Inline) [THT]"]
  Part1 = 12 NeoPixel Ring [part_number=1643]
  Neopixel3 = Adafruit RBG Smart Neopixel [package="DIP (Dual Inline) [THT]"]  # not connected
  Neopixel4 = Adafruit RBG Smart Neopixel [package="DIP (Dual Inline) [THT]"]

nets:
  N1: A1.Pin_2, A1.Pin_31, S1.Pin_3, S1.Pin_4, S2.Pin_3, S2.Pin_4, Neopixel1.+, Neopixel2.+, Part1.VDD, Neopixel4.+
  N2: A1.Pin_4, A1.Pin_30, A1.Pin_35, Neopixel1.G, Neopixel2.G, Part1.GND, Neopixel4.G
  N3: A1.Pin_12, Neopixel1.In
  N4: A1.Pin_19, S1.Pin_1, S1.Pin_2
  N5: A1.Pin_24, A1.Pin_36, S2.Pin_1, S2.Pin_2
  N6: Neopixel1.O, Neopixel2.In
  N7: Neopixel2.O, Part1.IN

custom parts:
  Particle - Photon2: The Photon 2 is a microcontroller and Wi-Fi networking developed by particle. Features: 802.11a/b/g/n Wi-Fi, 2.4 GHz and 5 GHz Integrated PCB antenna Integrated U.FL connector for external antenna Integrated RF switch BLE 5 using same antenna as Wi-Fi Realtek RTL8721DM MCU ARM Cortex M33 CPU, 200 MHz 2048 KB (2 MB) user application maximum size 3072 KB (3 MB) of RAM available to user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
  Pushbutton: A generic pushbutton.
  Pushbutton: A generic pushbutton.
  12 NeoPixel Ring: 12 ultra bright smart LED NeoPixels are arranged in a circle with 1.5" (37mm) outer diameter. The rings are 'chainable' - connect the output pin of one to the input pin of another. Use only one microcontroller pin to control as many as you can chain together! Each LED is addressable as the driver chip is inside the LED. Each one has ~18mA constant current drive so the color will be very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
